# Fritzing sketch Arduino Pro Nano V3 to Ra-01 (SX1278) (saved by Fritzing 0.9.3b)

parts:
  Part1 = Arduino Nano (Rev3.0)
  LoRa_Module1 = Ra-01 - LoRa Module SX1278 [part_number=SX1278]

nets:
  N1: Part1.D2, LoRa_Module1.DIO0
  N2: Part1.D3, LoRa_Module1.RESET
  N3: Part1.D8, LoRa_Module1.NSS
  N4: Part1.D11/MOSI, LoRa_Module1.MOSI
  N5: Part1.D12/MISO, LoRa_Module1.MISO
  GND: Part1.GND, LoRa_Module1.GND
  3V3: Part1.3V3, LoRa_Module1.3.3V
  N6: Part1.D13/SCK, LoRa_Module1.SCK

notes:
  BangGood Ra-01 (SX1278) Use only 3.3V
  NSS=CS (in SPI)

custom parts:
  Ra-01 - LoRa Module SX1278: The Ra-01 LoRa Module featuring the SX1278 engine by Semtech. Module by AI-Thinker. Module (Ra-01) specifications from: https://www.banggood.com/Ra-01-Smart-Electronics-SX1278-LoRa-Spread-Spectrum-Wireless-Module-Ultra-Far-10KM-433M-p-1130769.html Description: Power supply: DC1.8-3.7V(3.3V) Chip: SX1278 Frequency: 433Mhz Operating temperature: -40~+85°C On Sheild Description (may vary by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
