# Fritzing sketch Ra-01 Breakout Board (saved by Fritzing 0.9.3b)
circuit board: 3.72554cm x 2.73056cm

parts:
  J1 = female pin header, 8 pins [form="♀ (female)"]
  J2 = female pin header, 8 pins [form="♀ (female)"]
  LoRa_Module1 = Ra-01 - LoRa Module SX1278 [part_number=SX1278]

nets:
  N1: J1.pin1, LoRa_Module1.GND#1
  N2: J1.pin2, LoRa_Module1.NSS
  N3: J1.pin3, LoRa_Module1.MOSI
  N4: J1.pin4, LoRa_Module1.MISO
  N5: J1.pin5, LoRa_Module1.SCK
  N6: J1.pin6, LoRa_Module1.DIO5
  N7: J1.pin7, LoRa_Module1.DIO4
  N8: J1.pin8, LoRa_Module1.GND#8
  N9: J2.pin1, LoRa_Module1.ANT
  N10: J2.pin2, LoRa_Module1.GND#10
  N11: J2.pin3, LoRa_Module1.3.3V
  N12: J2.pin4, LoRa_Module1.RESET
  N13: J2.pin5, LoRa_Module1.DIO0
  N14: J2.pin6, LoRa_Module1.DIO1
  N15: J2.pin7, LoRa_Module1.DIO2
  N16: J2.pin8, LoRa_Module1.DIO3

notes:
  BangGood Ra-01 (SX1278) Use only 3.3V
  NSS=CS (in SPI)

custom parts:
  Ra-01 - LoRa Module SX1278: The Ra-01 LoRa Module featuring the SX1278 engine by Semtech. Module by AI-Thinker. Module (Ra-01) specifications from: https://www.banggood.com/Ra-01-Smart-Electronics-SX1278-LoRa-Spread-Spectrum-Wireless-Module-Ultra-Far-10KM-433M-p-1130769.html Description: Power supply: DC1.8-3.7V(3.3V) Chip: SX1278 Frequency: 433Mhz Operating temperature: -40~+85°C On Sheild Description (may vary by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
